# Fritzing sketch esquema (saved by Fritzing 0.9.3b)
breadboards: 1

parts:
  Componente1 = Photon
  DHT1 = DHT22 Humidity and Temperature Sensor
  D1 = LTE-302 [package=lte-302]
  R1 = PHOTOCELL [package=photocell-kit]
  R2 = Resistor [tolerance=±5% resistance=10k package=THT]
  R3 = Resistor [tolerance=±5% resistance=1k package=THT]
  R4 = Resistor [tolerance=±5% resistance=1k package=THT]

nets:
  N1: Componente1.A0, R1.P$1, R3.Pin_1
  N2: Componente1.A5, R1.P$2
  GND: Componente1.GND, DHT1.GND, D1.A, R3.Pin_0
  N3: Componente1.D1, DHT1.DATA, R2.Pin_1
  N4: Componente1.D5, R4.Pin_0
  3V3: Componente1.3V3, DHT1.VDD, R2.Pin_0
  N5: D1.C, R4.Pin_1
